// Logisim project PA1.circ as structural Verilog: 4 circuits, main circuit main
module main (
  input  [31:0] in_1,
  output [31:0] out_2
);

  wire and_1_out, and_2_out;
  wire [31:0] branch_1_out_2, multiplexer_1_out, r_type_1_out_2, ri_1_out_2;

  R_Type r_type_1 (.in_1(in_1), .out_2(r_type_1_out_2));
  and and_1 (and_1_out, ~in_1[26], ~in_1[27], ~in_1[28], ~in_1[29], ~in_1[30], ~in_1[31]);  // AND_Gate
  RI ri_1 (.in_1(in_1), .out_2(ri_1_out_2));
  Branch branch_1 (.in_1(in_1), .out_2(branch_1_out_2));
  and and_2 (and_2_out, in_1[26], ~in_1[27], ~in_1[28], ~in_1[29], ~in_1[30], ~in_1[31]);  // AND_Gate
  Multiplexer #(.width(32), .enable("false")) multiplexer_1 (
    .in0(ri_1_out_2), .in1(branch_1_out_2), .out(multiplexer_1_out), .sel(and_2_out));
  Multiplexer #(.width(32), .enable("false")) multiplexer_2 (
    .in0(multiplexer_1_out), .in1(r_type_1_out_2), .out(out_2), .sel(and_1_out));
endmodule

module R_Type (
  input  [31:0] in_1,
  output [31:0] out_2
);


  assign out_2 = in_1;
endmodule

// RI Type
module RI (
  input  [31:0] in_1,
  output [31:0] out_2
);


  assign out_2 = in_1;
endmodule

module Branch (
  input  [31:0] in_1,
  output [31:0] out_2
);


  assign out_2 = in_1;
endmodule
